# Fritzing sketch 아두이노 RC카_led (saved by Fritzing 0.8.7b)
breadboards: 1

parts:
  부품1 = Arduino Uno (Rev3)
  L298N1 = L298N DC motor driver
  M1 = DC Motor  # not connected
  M2 = DC Motor  # not connected
  M3 = DC Motor  # not connected
  M4 = DC Motor  # not connected
  부품2 = Bluetooth HC-06
  LED1 = LED - 5mm [color="White (4500K)" package="5 mm [THT]"]
  LED2 = LED - 5mm [color="White (4500K)" package="5 mm [THT]"]
  R1 = Resistor [tolerance=±5% resistance=330 package=THT]

nets:
  N1: 부품1.D8, LED2.anode
  N2: 부품1.D9_PWM, LED1.anode
  N3: 부품1.D10_PWM/SS, L298N1.ENA
  N4: 부품1.D11_PWM/MOSI, L298N1.ENB
  N5: 부품1.D12/MISO, 부품2.TXD
  N6: 부품1.D13/SCK, 부품2.RXD
  N7: 부품1.D2, L298N1.IN3
  N8: 부품1.D3_PWM, L298N1.IN4
  N9: 부품1.D4, L298N1.IN2
  N10: 부품1.D5_PWM, L298N1.IN1
  5V: 부품1.5V, L298N1.5V, 부품2.VCC
  GND: 부품1.GND, L298N1.GND, 부품2.GND, R1.Pin_0
  VIN: 부품1.VIN, L298N1.12V
  N11: LED1.cathode, LED2.cathode, R1.Pin_1

custom parts:
  L298N DC motor driver: 2x DC motor driver with 78M05 positive voltage regulator (7..35 V) L298N: max 46 V, 2 A Set 5 V Enable jumper to enable 5 V regultor (needed for the L298N) and +5 V output at screw terminal or supply external +5 V at screw terminal Set ENA and/or ENB to +5 V to enable motor permanently or supply ENA and/or ENB with PWM signal IN1 and IN2 set rotation directory for motor A (OUT1/OUT2) IN2 and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
